# Fritzing sketch Circuit_Ruche_ArduinoMKRWAN1310 (saved by Fritzing 0.9.3b)
breadboards: 1

parts:
  BME280 = Adafruit BME280 [part_number="Adafruit #2652"]
  Load_Combinator = SparkFun Load Sensor Combinator
  HX711_Load_Cell_Amplifier = Sparkfun load cell amplifier
  Load_Cell1 = Load Cell - Red/white/black/green
  Arduino_MKR1310_WAN = Arduino MKR WAN 1310
  DHT22 = DHT22 Humidity and Temperature Sensor
  R3 = Resistor [tolerance=±5% resistance=220 package=THT]
  Composant1 = Adafruit BQ24074 Solar-DC-USB Lipo Charger  # not connected

nets:
  GND: BME280.GND, HX711_Load_Cell_Amplifier.Pin_6, Arduino_MKR1310_WAN.GND, DHT22.GND
  VCC: BME280.VCC, HX711_Load_Cell_Amplifier.Pin_9, Arduino_MKR1310_WAN.+3V3, DHT22.VDD
  N1: BME280.SDI/SDA, Arduino_MKR1310_WAN.D11/MOSI, Arduino_MKR1310_WAN.+5V
  N2: BME280.SCK/SCL, Arduino_MKR1310_WAN.D12~/MISO
  N3: Load_Combinator.N$1, Load_Cell1.wire3
  N4: Load_Combinator.2, Load_Cell1.wire2
  N5: Load_Combinator.E+, HX711_Load_Cell_Amplifier.Pin_1, Load_Cell1.wire1
  N6: Load_Combinator.E-, HX711_Load_Cell_Amplifier.Pin_2
  N7: Load_Combinator.A-, HX711_Load_Cell_Amplifier.Pin_3
  N8: Load_Combinator.A+, HX711_Load_Cell_Amplifier.Pin_4
  N9: Load_Combinator.5, HX711_Load_Cell_Amplifier.Pin_5
  N10: HX711_Load_Cell_Amplifier.Pin_7, Arduino_MKR1310_WAN.D4
  N11: HX711_Load_Cell_Amplifier.Pin_8, Arduino_MKR1310_WAN.D5~
  N12: Arduino_MKR1310_WAN.D2, DHT22.DATA
  N13: Arduino_MKR1310_WAN.A3, R3.Pin_1

notes:
  On peut brancher jusqu'à 4 jauges de contraintes sur le "Load Combinator" en suivant le même branchement que celui effectué ci-contre.
  Load Combinator
  LR : LOWER RIGHT- Bas droit
  LL : LOWER LEFT - Bas gauche
  UR : UPPER RIGHT - Haut droit
  UL : UPPER LEFT - Haut gauche
  Batterie
  Panneau solaire
  Mesure de l'ensoleillement via panneau

custom parts:
  Adafruit BME280: Bosch has stepped up their game with their new BME280 sensor, an environmental sensor with temperature, barometric pressure and humidity! This sensor is great for all sorts of indoor environmental sensing and can even be used in both I2C and SPI! This precision sensor from Bosch is the best low-cost sensing solution for measuring humidity with ±3% accuracy, barometric pressure with ±1 hPa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
  Sparkfun load cell amplifier: The SparkFun Load Cell Amplifier is a small breakout board for the HX711 IC that allows you to easily read load cells to measure weight.
  Load Cell - Red/white/black/green: A rectangle load cell/weighting pressure Sensor with four wires - Red, white, black, green. Normally corresponding with E+, E-, A+, A- respectively.
  Arduino MKR WAN 1310: The Arduino MKR WAN 1310 board provides a practical and cost effective solution to add LoRa® connectivity to projects requiring low power. This open source board can be connected to: the Arduino IoT Cloud, your own LoRa® network using the Arduino LoRa® PRO Gateway, existing LoRaWAN™ infrastructure like The Things Network, or even other boards using the direct connectivity mode.
